// Logisim project LogisimProject.circ as structural Verilog: 6 circuits, main circuit sixtyFourRegisterRam
module oneBitRegister (
  input  inBit,
  input  load,
  output outBit
);

  wire clock_1_out, multiplexer_1_out;

  D_Flip_Flop DFF (.D(multiplexer_1_out), .clk(clock_1_out), .Q(outBit));  // open: Qn, preset, reset
  Multiplexer multiplexer_1 (.in0(outBit), .in1(inBit), .out(multiplexer_1_out), .sel(load));
  Clock clock_1 (.out(clock_1_out));

  // Notes on the sheet:
  //   one bit register
endmodule

module sixteenBitRegister (
  input  [15:0] inSixteenBit,
  input  load,
  output [15:0] outSixteen
);

  oneBitRegister in8 (.inBit(inSixteenBit[8]), .load(load), .outBit(outSixteen[8]));
  oneBitRegister in9 (.inBit(inSixteenBit[9]), .load(load), .outBit(outSixteen[9]));
  oneBitRegister in10 (.inBit(inSixteenBit[10]), .load(load), .outBit(outSixteen[10]));
  oneBitRegister in11 (.inBit(inSixteenBit[11]), .load(load), .outBit(outSixteen[11]));
  oneBitRegister in12 (.inBit(inSixteenBit[12]), .load(load), .outBit(outSixteen[12]));
  oneBitRegister in13 (.inBit(inSixteenBit[13]), .load(load), .outBit(outSixteen[13]));
  oneBitRegister in14 (.inBit(inSixteenBit[14]), .load(load), .outBit(outSixteen[14]));
  oneBitRegister in15 (.inBit(inSixteenBit[15]), .load(load), .outBit(outSixteen[15]));
  oneBitRegister in0 (.inBit(inSixteenBit[0]), .load(load), .outBit(outSixteen[0]));
  oneBitRegister in1 (.inBit(inSixteenBit[1]), .load(load), .outBit(outSixteen[1]));
  oneBitRegister in2 (.inBit(inSixteenBit[2]), .load(load), .outBit(outSixteen[2]));
  oneBitRegister in3 (.inBit(inSixteenBit[3]), .load(load), .outBit(outSixteen[3]));
  oneBitRegister in4 (.inBit(inSixteenBit[4]), .load(load), .outBit(outSixteen[4]));
  oneBitRegister in5 (.inBit(inSixteenBit[5]), .load(load), .outBit(outSixteen[5]));
  oneBitRegister in6 (.inBit(inSixteenBit[6]), .load(load), .outBit(outSixteen[6]));
  oneBitRegister in7 (.inBit(inSixteenBit[7]), .load(load), .outBit(outSixteen[7]));
endmodule

module eightRegisterRam (
  input  load,
  input  [15:0] inEightRegisterRam,
  input  [2:0] address,
  output [15:0] outEightRegisterRam
);

  wire demultiplexer_1_out0, demultiplexer_1_out1, demultiplexer_1_out2, demultiplexer_1_out3,
       demultiplexer_1_out4, demultiplexer_1_out5, demultiplexer_1_out6, demultiplexer_1_out7;
  wire [15:0] demultiplexer_2_out0, demultiplexer_2_out1, demultiplexer_2_out2, demultiplexer_2_out3,
       demultiplexer_2_out4, demultiplexer_2_out5, demultiplexer_2_out6, demultiplexer_2_out7,
       register0_outsixteen, register1_outsixteen, register2_outsixteen, register3_outsixteen,
       register4_outsixteen, register5_outsixteen, register6_outsixteen, register7_outsixteen;

  Demultiplexer #(.select(3)) demultiplexer_1 (
    .out0(demultiplexer_1_out0), .out1(demultiplexer_1_out1), .out2(demultiplexer_1_out2),
    .out3(demultiplexer_1_out3), .out4(demultiplexer_1_out4), .out5(demultiplexer_1_out5),
    .out6(demultiplexer_1_out6), .out7(demultiplexer_1_out7), .in(load), .sel(address));
  Demultiplexer #(.select(3), .width(16)) demultiplexer_2 (
    .out0(demultiplexer_2_out0), .out1(demultiplexer_2_out1), .out2(demultiplexer_2_out2),
    .out3(demultiplexer_2_out3), .out4(demultiplexer_2_out4), .out5(demultiplexer_2_out5),
    .out6(demultiplexer_2_out6), .out7(demultiplexer_2_out7), .in(inEightRegisterRam), .sel(address));
  sixteenBitRegister register0 (
    .inSixteenBit(demultiplexer_2_out0), .load(demultiplexer_1_out0), .outSixteen(register0_outsixteen));
  sixteenBitRegister register1 (
    .inSixteenBit(demultiplexer_2_out1), .load(demultiplexer_1_out1), .outSixteen(register1_outsixteen));
  sixteenBitRegister register2 (
    .inSixteenBit(demultiplexer_2_out2), .load(demultiplexer_1_out2), .outSixteen(register2_outsixteen));
  sixteenBitRegister register3 (
    .inSixteenBit(demultiplexer_2_out3), .load(demultiplexer_1_out3), .outSixteen(register3_outsixteen));
  sixteenBitRegister register4 (
    .inSixteenBit(demultiplexer_2_out4), .load(demultiplexer_1_out4), .outSixteen(register4_outsixteen));
  sixteenBitRegister register5 (
    .inSixteenBit(demultiplexer_2_out5), .load(demultiplexer_1_out5), .outSixteen(register5_outsixteen));
  sixteenBitRegister register6 (
    .inSixteenBit(demultiplexer_2_out6), .load(demultiplexer_1_out6), .outSixteen(register6_outsixteen));
  sixteenBitRegister register7 (
    .inSixteenBit(demultiplexer_2_out7), .load(demultiplexer_1_out7), .outSixteen(register7_outsixteen));
  Multiplexer #(.select(3), .width(16)) multiplexer_1 (
    .in0(register0_outsixteen), .in1(register1_outsixteen), .in2(register2_outsixteen),
    .in3(register3_outsixteen), .in4(register4_outsixteen), .in5(register5_outsixteen),
    .in6(register6_outsixteen), .in7(register7_outsixteen), .out(outEightRegisterRam), .sel(address));
endmodule

module sixtyFourRegisterRam (
  input  [5:0] address,
  input  load,
  input  [15:0] inp,
  output [15:0] out_4
);

  wire clock_1_out;

  RAM #(.addrWidth(6), .dataWidth(16), .enables("line"), .\type ("nonvolatile")) ram_1 (
    .addr(address), .we(load), .clk(clock_1_out), .din(inp), .dout(out_4));
  Clock clock_1 (.out(clock_1_out));
endmodule

module fiveHundredTwelveRegisterRam (
  input  [8:0] address,
  input  load,
  input  [15:0] inp,
  output [15:0] outp
);

  wire clock_1_out;

  RAM #(.addrWidth(9), .dataWidth(16), .enables("line"), .\type ("nonvolatile")) ram_1 (
    .addr(address), .we(load), .clk(clock_1_out), .din(inp), .dout(outp));
  Clock clock_1 (.out(clock_1_out));
endmodule

module sixteenBitCounter (
  input  inc,
  input  [15:0] inpt,
  input  load,
  input  reset,
  output [15:0] outpt
);

  wire clock_1_out;
  wire [15:0] adder_1_out, multiplexer_1_out, multiplexer_2_out, multiplexer_3_out;

  Multiplexer #(.width(16)) multiplexer_1 (.in0(outpt), .in1(adder_1_out), .out(multiplexer_1_out), .sel(inc));
  Multiplexer #(.width(16)) multiplexer_2 (.in0(multiplexer_1_out), .in1(inpt), .out(multiplexer_2_out), .sel(load));
  Multiplexer #(.width(16)) multiplexer_3 (
    .in0(multiplexer_2_out), .in1({16{1'b0}}), .out(multiplexer_3_out), .sel(reset));
  Register #(.width(16)) register_1 (.D(multiplexer_3_out), .clk(clock_1_out), .Q(outpt));  // open: en, clr
  Clock clock_1 (.out(clock_1_out));
  Adder #(.width(16)) adder_1 (.a(outpt), .b(16'h1), .out(adder_1_out));  // open: cin, cout
endmodule
